# Fritzing sketch frescobol-nano-bt (saved by Fritzing 0.9.3b)
circuit board: 5.00258cm x 6.11955cm

parts:
  BUT-ESQ = Momentary Switch [package=ksa_sealed_tac_switch]
  BUT-DIR = Momentary Switch [package=ksa_sealed_tac_switch]
  TP1 = TP4056 [chip_label=TP4056 package="DIP (Dual Inline) [THT]"]
  Part5 = Bluetooth HC-05 Macho
  BUT-CFG = Momentary Switch [package=ksa_sealed_tac_switch]
  SW1 = DIP SWITCH [package=dipswitch-02]
  BAT+ = male pin header, 1 pin [form="♂ (male)"]
  BAT- = male pin header, 1 pin [form="♂ (male)"]
  Audio-11-B = male pin header, 1 pin [form="♂ (male)"]
  Audio-GND-B = male pin header, 1 pin [form="♂ (male)"]
  ESQ-3-A = male pin header, 1 pin [form="♂ (male)"]
  ESQ-GND-A = male pin header, 1 pin [form="♂ (male)"]
  DIR-2-A = male pin header, 1 pin [form="♂ (male)"]
  DIR-GND-B = male pin header, 1 pin [form="♂ (male)"]
  R1 = Resistor [tolerance=±5% resistance=2.2k package=THT]
  R2 = Resistor [tolerance=±5% resistance=1k package=THT]
  Part4 = Arduino Nano (Rev3.0) (ICSP)
  DIR-2-B = male pin header, 1 pin [form="♂ (male)"]
  DIR-GND-B_2 = male pin header, 1 pin [form="♂ (male)"]
  ESQ-3-B = male pin header, 1 pin [form="♂ (male)"]
  ESQ-GND-B = male pin header, 1 pin [form="♂ (male)"]
  Audio-11-A = male pin header, 1 pin [form="♂ (male)"]
  Audio-GND-A = male pin header, 1 pin [form="♂ (male)"]

nets:
  N1: BUT-ESQ.2, ESQ-3-A.pin1, Part4.D3, ESQ-3-B.pin1
  N2: BUT-ESQ.3, Audio-GND-B.pin1, Audio-GND-A.pin1
  N3: BUT-ESQ.4, BUT-DIR.3, TP1.pin5, ESQ-GND-A.pin1, ESQ-GND-B.pin1
  N4: BUT-DIR.2, DIR-2-A.pin1, Part4.D2, DIR-2-B.pin1
  GND: BUT-DIR.4, Part5.GND, BUT-CFG.1, BAT-.pin1, DIR-GND-B.pin1, R1.Pin_0, Part4.GND, DIR-GND-B_2.pin1
  N5: TP1.pin4, SW1.3, BAT+.pin1
  N6: Part5.TXD, Part4.D0/RX
  N7: Part5.RXD, R1.Pin_1, R2.Pin_1
  N8: Part5.VCC, SW1.4
  N9: BUT-CFG.4, Part4.D4
  N10: SW1.1, SW1.2, Part4.5V
  N11: Audio-11-B.pin1, Part4.D11/MOSI, Audio-11-A.pin1
  N12: R2.Pin_0, Part4.D1/TX

custom parts:
  TP4056: A DIP stand-in part for whatever IC you want. With 6 pins on a 300mil dual inline package (DIP) footprint.
