# Fritzing sketch frescobol-nano (saved by Fritzing 0.9.3b)
circuit board: 5.20911cm x 1.976cm
perfboards: 1

parts:
  S1 = Momentary Switch [package=ksa_sealed_tac_switch]
  S2 = Momentary Switch [package=ksa_sealed_tac_switch]
  Part2 = TRRS 3.5mm Jack Breakout
  Part4 = Arduino Nano (Rev3.0) (ICSP)

nets:
  N1: S1.1, Part4.D2
  N2: S1.4, S2.4, Part2.TIP, Part4.GND
  N3: S2.2, Part4.D3
  N4: Part2.SLEEVE, Part2.RING2, Part4.D11/MOSI
