# Fritzing sketch frescobol (saved by Fritzing 0.9.3b)
circuit board: 9.07452cm x 5.69509cm
perfboards: 1

parts:
  Part1 = Arduino Mega 2560 (Rev3)
  S1 = Momentary Switch [package=ksa_sealed_tac_switch]
  S2 = Momentary Switch [package=ksa_sealed_tac_switch]
  Part2 = TRRS 3.5mm Jack Breakout
  J1 = female pin header, 2 pins [form="♀ (female)"]
  R2 = Resistor [tolerance=±5% resistance=1k package="0603 [SMD]"]
  R3 = Resistor [tolerance=±5% resistance=470 package="0603 [SMD]"]
  Part3 = Bluetooth HC-05 Macho
  R4 = Resistor [tolerance=±5% resistance=2k package="0603 [SMD]"]
  SW1 = DIP SWITCH [package=dipswitch-02]
  R5 = Resistor [tolerance=±5% resistance=1k package="0603 [SMD]"]

nets:
  N1: Part1.D21/SCL, Part1.SCL, S2.1
  N2: Part1.D20/SDA, Part1.SDA, S1.3
  GND: Part1.GND, S1.2, S2.4, Part2.TIP, Part3.GND
  N3: Part1.D11_PWM, R2.Pin_0
  N4: Part1.D10_PWM, Part2.SLEEVE, Part2.RING2
  3V3: Part1.3V3, Part3.VCC
  N5: Part1.D29, R3.Pin_0
  N6: J1.pin1, R2.Pin_1
  N7: J1.pin2, R3.Pin_1
  N8: Part3.TXD, SW1.1
  N9: Part3.RXD, R5.Pin_0
  N10: R4.Pin_1, SW1.4
