# Fritzing sketch frescobol-mega-bt (saved by Fritzing 0.9.3b)
circuit board: 10.16cm x 5.36194cm

parts:
  S1 = Momentary Switch [package=ksa_sealed_tac_switch]
  S2 = Momentary Switch [package=ksa_sealed_tac_switch]
  TP1 = TP4056 [chip_label=TP4056 package="DIP (Dual Inline) [THT]"]
  Part5 = Bluetooth HC-05 Macho
  S3 = Momentary Switch [package=ksa_sealed_tac_switch]
  SW1 = DIP SWITCH [package=dipswitch-02]
  BAT+ = male pin header, 1 pin [form="♂ (male)"]
  BAT- = male pin header, 1 pin [form="♂ (male)"]
  Audio-11-B = male pin header, 1 pin [form="♂ (male)"]
  Audio-GND-B = male pin header, 1 pin [form="♂ (male)"]
  ESQ-3-A = male pin header, 1 pin [form="♂ (male)"]
  ESQ-GND-A = male pin header, 1 pin [form="♂ (male)"]
  DIR-2-A = male pin header, 1 pin [form="♂ (male)"]
  DIR-GND-A = male pin header, 1 pin [form="♂ (male)"]
  R-GND = Resistor [tolerance=±5% resistance=2.2k package=THT]
  R-TX = Resistor [tolerance=±5% resistance=1k package=THT]
  DIR-2-B = male pin header, 1 pin [form="♂ (male)"]
  DIR-GND-B = male pin header, 1 pin [form="♂ (male)"]
  ESQ-3-B = male pin header, 1 pin [form="♂ (male)"]
  ESQ-GND-B = male pin header, 1 pin [form="♂ (male)"]
  Part6 = Arduino Mega 2560 (Rev3)
  Audio-11-A = male pin header, 1 pin [form="♂ (male)"]
  Audio-GND-A = male pin header, 1 pin [form="♂ (male)"]
  R-29 = Resistor [tolerance=±5% resistance=470 package=THT]
  R-11 = Resistor [tolerance=±5% resistance=1k package=THT]
  VIDEO = female pin header, 2 pins [form="♀ (female)"]

nets:
  N1: S1.2, ESQ-3-A.pin1, ESQ-3-B.pin1, Part6.D3_PWM
  N2: S1.3, TP1.pin5
  N3: S1.4, S2.3, Part5.GND, S3.1, ESQ-GND-A.pin1, DIR-GND-A.pin1, DIR-GND-B.pin1, ESQ-GND-B.pin1
  N4: S2.1, S2.2, DIR-2-A.pin1, DIR-2-B.pin1, Part6.D2_PWM
  N5: S2.4, R-GND.Pin_0, VIDEO.pin2
  N6: TP1.pin4, SW1.4, BAT+.pin1
  N7: Part5.TXD, Part6.D0_RX0
  N8: Part5.RXD, R-GND.Pin_1, R-TX.Pin_1
  N9: Part5.VCC, SW1.3
  N10: S3.2, BAT-.pin1, Audio-GND-B.pin1, Audio-GND-A.pin1
  N11: S3.4, Part6.D4_PWM
  N12: SW1.1, SW1.2, Part6.5V
  N13: Audio-11-B.pin1, Part6.D10_PWM, Audio-11-A.pin1
  N14: R-TX.Pin_0, Part6.D1_TX0
  N15: Part6.D11_PWM, R-11.Pin_0
  N16: Part6.D29, R-29.Pin_0
  N17: R-29.Pin_1, R-11.Pin_1, VIDEO.pin1

custom parts:
  TP4056: A DIP stand-in part for whatever IC you want. With 6 pins on a 300mil dual inline package (DIP) footprint.
