# Fritzing sketch frescobol-mega (saved by Fritzing 0.9.3b)
circuit board: 9.07452cm x 5.69509cm

parts:
  Part1 = Arduino Mega 2560 (Rev3)
  S1 = Momentary Switch [package=ksa_sealed_tac_switch]
  S2 = Momentary Switch [package=ksa_sealed_tac_switch]
  Part2 = TRRS 3.5mm Jack Breakout
  Part3 = Bluetooth HC-05 Macho
  C3 = Electrolytic Capacitor [capacitance=22µF package="0605 [SMD, electrolytic]"]  # not connected
  J1 = female pin header, 2 pins [form="♀ (female)"]
  J2 = male pin header, 2 pins [form="♂ (male)"]
  R3 = Resistor [tolerance=±5% resistance=470 package=THT]
  R4 = Resistor [tolerance=±5% resistance=2k package=THT]
  R2 = Resistor [tolerance=±5% resistance=1k package=THT]
  R5 = Resistor [tolerance=±5% resistance=1k package=THT]
  C7 = Electrolytic Capacitor [capacitance=22µF package="0605 [SMD, electrolytic]"]
  J3 = male pin header, 2 pins [form="♂ (male)"]

nets:
  N1: Part1.D21/SCL, S1.3
  N2: Part1.D20/SDA, Part1.SDA, S2.2
  GND: Part1.GND, S1.2, S2.4, Part2.SLEEVE, Part3.GND, J1.pin2, R4.Pin_0, C7.-
  N3: Part1.D11_PWM, R2.Pin_0
  N4: Part1.D10_PWM, Part2.RING1, Part2.TIP
  N5: Part1.RESET, J3.pin2
  5V: Part1.5V, Part3.VCC
  N6: Part1.D0_RX0, J2.pin1
  N7: Part1.D1_TX0, R5.Pin_1
  N8: Part1.D29, R3.Pin_0
  N9: Part3.TXD, J2.pin2
  N10: Part3.RXD, R4.Pin_1, R5.Pin_0
  N11: J1.pin1, R3.Pin_1, R2.Pin_1
  N12: C7.+, J3.pin1
